# Fritzing sketch Joystick (saved by Fritzing 0.9.3b)
breadboards: 1

parts:
  Componente1 = Thumb Joystick
  Componente2 = Arduino Uno (Rev3)
  R1 = Resistor [tolerance=±5% resistance=220 package="2512 [SMD]"]
  J1 = Piezo Speaker
  LED1 = LEDs [package=led10mm]
  LED2 = LEDs [package=led10mm]
  LED3 = LEDs [package=led10mm]
  LED4 = LEDs [package=led10mm]

nets:
  GND: Componente1.GND, Componente2.GND, J1.pin2, LED1.C, LED2.C, LED3.C, LED4.C
  N1: Componente1.SEL, Componente2.5V, R1.Pin_0
  N2: Componente1.HORZ, Componente2.A1
  N3: Componente1.VERT, Componente2.A2
  N4: Componente1.VCC, Componente2.D2, R1.Pin_1
  N5: Componente2.D8, LED4.A
  N6: Componente2.D9_PWM, LED3.A
  N7: Componente2.D5_PWM, LED1.A
  N8: Componente2.D6_PWM, LED2.A
  N9: Componente2.D7, J1.pin1
