# Fritzing sketch Sensor_ultrasom (saved by Fritzing 0.9.3b)
breadboards: 1

parts:
  hc-sr1 = hc-sr04
  Componente1 = Arduino Uno (Rev3)
  J1 = Piezo Speaker

nets:
  VCC: hc-sr1.VCC, Componente1.5V
  N1: hc-sr1.Trig, Componente1.D12/MISO
  N2: hc-sr1.Echo, Componente1.D11_PWM/MOSI
  GND: hc-sr1.GND, Componente1.GND, J1.pin2
  N3: Componente1.D8, J1.pin1
