# Fritzing sketch display7 (saved by Fritzing 0.9.3b)
breadboards: 1

parts:
  Componente1 = Arduino Uno (Rev3)
  DI1 = 7-Segment LED Display [package=THT]
  R1 = Resistor [tolerance=±5% resistance=220 package="2010 [SMD]"]

nets:
  N1: Componente1.D8, DI1.cathodeD
  N2: Componente1.D9_PWM, DI1.cathodeE
  N3: Componente1.D10_PWM/SS, DI1.cathodeC
  N4: Componente1.D11_PWM/MOSI, DI1.cathodeB
  N5: Componente1.D12/MISO, DI1.cathodeA
  N6: Componente1.D6_PWM, DI1.cathodeG
  N7: Componente1.D7, DI1.cathodeF
  N8: DI1.commAnode#7, R1.Pin_0
