# Fritzing sketch encoder_rotativo___led_rgb (saved by Fritzing 0.9.3b)
breadboards: 1

parts:
  Componente1 = Arduino Uno (Rev3)
  LED1 = RGB LED (com. cathode, rgb) [package="5 mm [THT]"]
  SW1 = ENCODER_RGB_CA [package=encoder_led_3]

nets:
  N1: Componente1.D8, LED1.green_anode
  N2: Componente1.D9_PWM, LED1.common_cathode
  N3: Componente1.D10_PWM/SS, LED1.red_anode
  N4: Componente1.D4, SW1.-R
  N5: Componente1.D5_PWM, SW1.-G
  N6: Componente1.GND, LED1.blue_anode, SW1.SW
  N7: SW1.-B, SW1.+, SW1.A, SW1.C
