# Fritzing sketch gas_detector (saved by Fritzing 0.9.3b)
breadboards: 1

parts:
  Componente1 = Arduino Uno (Rev3)
  U1 = GAS_SENSOR [package=mq-3]
  J1 = Piezo Speaker
  LED1 = LED - 5mm [color="Red (633nm)" package="5 mm [THT]"]
  LED2 = LED - 5mm [color="Red (633nm)" package="5 mm [THT]"]

nets:
  N1: Componente1.A5/SCL, U1.B1
  N2: Componente1.D5_PWM, LED2.anode
  N3: Componente1.D6_PWM, LED1.anode
  N4: Componente1.D7, J1.pin2
  N5: J1.pin1, LED1.cathode, LED2.cathode
