# Fritzing sketch lcd (saved by Fritzing 0.9.3b)
breadboards: 1

parts:
  Componente1 = Arduino Uno (Rev3)
  LCD1 = LCD screen
  R1 = Resistor [tolerance=±5% resistance=220 package="2010 [SMD]"]

nets:
  N1: Componente1.D8, LCD1.DB2
  N2: Componente1.D9_PWM, LCD1.DB3
  N3: Componente1.D10_PWM/SS, LCD1.DB4
  N4: Componente1.D11_PWM/MOSI, LCD1.DB5
  N5: Componente1.D12/MISO, LCD1.DB6
  N6: Componente1.D13/SCK, LCD1.DB7
  N7: Componente1.D2, LCD1.RS
  N8: Componente1.D3_PWM, LCD1.R/W
  N9: Componente1.D4, LCD1.E
  N10: Componente1.D6_PWM, LCD1.DB0
  N11: Componente1.D7, LCD1.DB1
  5V: Componente1.5V, LCD1.VDD, R1.Pin_1
  GND: Componente1.GND, LCD1.VSS, LCD1.V0, LCD1.LED-
  N12: LCD1.LED+, R1.Pin_0
